# Fritzing sketch Bank (saved by Fritzing 0.9.3b)
breadboards: 1

parts:
  Keypad4x1 = Keypad Membran 4x4
  Onderdeel1 = RFID-RC522-v2
  Onderdeel2 = Arduino Uno (Rev3) - ICSP
  U1 = NodeMCU V3.0
  M1 = DC Motor
  IC1 = H-Bridge [package=THT]
  Onderdeel3 = Thermal Printer

nets:
  N1: Keypad4x1.Pin1, Onderdeel2.A3
  N2: Keypad4x1.Pin2, Onderdeel2.A2
  N3: Keypad4x1.Pin3, Onderdeel2.A1
  N4: Keypad4x1.Pin4, Onderdeel2.D3_PWM
  N5: Keypad4x1.Pin5, Onderdeel2.D4
  N6: Keypad4x1.Pin6, Onderdeel2.D5_PWM
  N7: Keypad4x1.Pin7, Onderdeel2.D6_PWM
  N8: Keypad4x1.Pin8, Onderdeel2.D7
  N9: Onderdeel1.SDA, Onderdeel2.D10_PWM/SS
  N10: Onderdeel1.SCK, Onderdeel2.D13/SCK
  N11: Onderdeel1.MOSI, Onderdeel2.ICSP_MOSI, Onderdeel2.D11_PWM/MOSI
  N12: Onderdeel1.MISO, Onderdeel2.D12/MISO
  GND: Onderdeel1.GND, Onderdeel2.GND, IC1.GND1, IC1.GND2, IC1.GND3, IC1.GND4, Onderdeel3.GND#2
  N13: Onderdeel1.RST, Onderdeel2.D9_PWM
  3.3V: Onderdeel1.3.3V, Onderdeel2.3V3
  N14: Onderdeel2.A4/SDA, U1.D2
  N15: Onderdeel2.A5/SCL, U1.D1
  N16: Onderdeel2.D8, Onderdeel3.RXD
  N17: Onderdeel2.D2, Onderdeel3.TXD
  N18: Onderdeel2.5V, IC1.VCC2, IC1.3_4EN, IC1.VCC1
  N19: U1.D5, IC1.2A
  N20: U1.D6, IC1.1A
  N21: U1.D7, IC1.1_2EN
  N22: M1.pin_1, IC1.1Y
  N23: M1.pin_2, IC1.2Y

notes:
  Muur-adapter

custom parts:
  Keypad Membran 4x4: Membrane Keypad 4x4 Matrix
  RFID-RC522-v2: A simple China made RFID-RC522 Reader; do check the pin labels, as this is a MFRC522 based clone.
  NodeMCU V3.0: NodeMcu V3 Lua WIFI Development Board
